# Fritzing sketch ToyTimer555 (saved by Fritzing 0.9.2b)
breadboards: 1

parts:
  TS555CN = 555 Timer [package="SO8 [SMD]"]
  2N3904 = NPN-Transistor [package="TO92 [THT]"]
  R1 = Resistor [tolerance=±5% resistance=10k package=THT]
  LED_3_2V = smd LED [color="White (4500K)" package="0805 [SMD]"]
  part = Resistor [tolerance=±5% resistance=5.6m package=THT]
  C1 = Electrolytic Capacitor [capacitance=22µF package="100 mil [THT, electrolytic]"]
  S1 = Pushbutton [package="[THT]"]
  C2 = Ceramic Capacitor [capacitance=100pF package="100 mil [THT, multilayer]"]
  R3 = Resistor [tolerance=±5% resistance=100k package=THT]
  C3 = Ceramic Capacitor [capacitance=8.2nF package="100 mil [THT, multilayer]"]
  R4 = Resistor [tolerance=±5% resistance=33k package=THT]
  D1 = Rectifier Diode [part_number=1N4001 package="300 mil [THT]"]

nets:
  GND: TS555CN.Pin_1, 2N3904.E, C1.-, S1.Pin_4, C2.0
  N1: TS555CN.Pin_2, C3.0, R4.Pin_0, D1.anode
  N2: TS555CN.Pin_3, R1.Pin_0
  3V: TS555CN.Pin_4, TS555CN.Pin_8, LED_3_2V.anode, part.Pin_0, R3.Pin_1, R4.Pin_1, D1.cathode
  N3: TS555CN.Pin_5, C2.1
  N4: TS555CN.Pin_6, TS555CN.Pin_7, part.Pin_1, C1.+
  N5: 2N3904.B, R1.Pin_1
  N6: 2N3904.C, LED_3_2V.cathode
  N7: S1.Pin_1, S1.Pin_2, R3.Pin_0, C3.1
